# Fritzing sketch arduino wiring (saved by Fritzing 0.9.3b)
breadboards: 1

parts:
  Part1 = Arduino Uno (Rev3)
  hc-sr1 = hc-sr04
  hc-sr2 = hc-sr04
  hc-sr3 = hc-sr04
  GY1 = GY-80

nets:
  N1: Part1.A4/SDA, GY1.SDA
  N2: Part1.A5/SCL, GY1.SCL
  N3: Part1.D8, hc-sr1.Echo
  N4: Part1.D5_PWM, hc-sr1.Trig, hc-sr2.Trig, hc-sr3.Trig
  N5: Part1.D6_PWM, hc-sr3.Echo
  N6: Part1.D7, hc-sr2.Echo
  VCC: Part1.5V, hc-sr1.VCC, hc-sr2.VCC, hc-sr3.VCC, GY1.VCC_IN
  GND: Part1.GND, hc-sr1.GND, hc-sr2.GND, hc-sr3.GND, GY1.GND

custom parts:
  GY-80: Placa GY-80 basada en conjunto de giroscopios L3G4200D + acelerómetros ADXL345 + magnetómetro HMC5883L + sensor barométrico BMP085
